// Logisim project TicTacToe.circ as structural Verilog: 6 circuits, main circuit NOR SR Latch
module main (
);

  wire C, CS1, CS2, CS3, CS4, CS5, CS6, CS7, CS8, CS9, game_over_1_t, game_over_1_w1, game_over_1_w2, L1, L2,
       L3, L4, L5, L6, L7, L8, L9, not_1_out, P11, P12, P13, P14, P15, P16, P17, P18, P19, P21, P22, P23,
       P24, P25, P26, P27, P28, P29, R, S1, S2, S3, S4, S5, S6, S7, S8, S9, W;

  LED led_1 (.in(P21));
  LED led_2 (.in(P11));
  LED led_3 (.in(P24));
  LED led_4 (.in(P14));
  LED led_5 (.in(P27));
  LED led_6 (.in(P17));
  LED led_7 (.in(P12));
  LED led_8 (.in(P15));
  LED led_9 (.in(P18));
  LED led_10 (.in(P22));
  LED led_11 (.in(P25));
  LED led_12 (.in(P28));
  xor odd_parity_1 (C, L1, L2, L3, L4, L5, L6, L7, L8, L9);
  LED led_13 (.in(P13));
  LED led_14 (.in(P23));
  LED led_15 (.in(P16));
  LED led_16 (.in(P26));
  LED led_17 (.in(P29));
  LED led_18 (.in(P19));
  Button button_1 (.out(R));
  Cell cell_1 (.R(R), .S(S1), .C(C), .CS(CS1), .P1(P11), .P2(P21), .L(L1));
  Cell cell_2 (.R(R), .S(S4), .C(C), .CS(CS4), .P1(P14), .P2(P24), .L(L4));
  Cell cell_3 (.R(R), .S(S7), .C(C), .CS(CS7), .P1(P17), .P2(P27), .L(L7));
  Cell cell_4 (.R(R), .S(S2), .C(C), .CS(CS2), .P1(P12), .P2(P22), .L(L2));
  Cell cell_5 (.R(R), .S(S5), .C(C), .CS(CS5), .P1(P15), .P2(P25), .L(L5));
  Cell cell_6 (.R(R), .S(S8), .C(C), .CS(CS8), .P1(P18), .P2(P28), .L(L8));
  Game_Over game_over_1 (
    .L1(L1), .L2(L2), .L3(L3), .L4(L4), .L5(L5), .L6(L6), .L7(L7), .L8(L8), .L9(L9), .W(W), .C(C),
    .T(game_over_1_t), .W1(game_over_1_w1), .W2(game_over_1_w2), .R(R));
  LED led_19 (.in(C));
  LED led_20 (.in(not_1_out));
  not not_1 (not_1_out, C);
  Cell cell_7 (.R(R), .S(S3), .C(C), .CS(CS3), .P1(P13), .P2(P23), .L(L3));
  Cell cell_8 (.R(R), .S(S6), .C(C), .CS(CS6), .P1(P16), .P2(P26), .L(L6));
  Cell cell_9 (.R(R), .S(S9), .C(C), .CS(CS9), .P1(P19), .P2(P29), .L(L9));
  LED led_21 (.in(game_over_1_w1));
  LED led_22 (.in(game_over_1_t));
  LED led_23 (.in(game_over_1_w2));
  Button button_2 (.out(S1));
  Button button_3 (.out(S4));
  Button button_4 (.out(S7));
  Button button_5 (.out(S2));
  Button button_6 (.out(S5));
  Button button_7 (.out(S8));
  Winner winner_1 (
    .out_10(W), .CS1(CS9), .CS2(CS8), .CS3(CS7), .CS4(CS6), .CS5(CS5), .CS6(CS4), .CS7(CS3), .CS8(CS2),
    .CS9(CS1));
  Button button_8 (.out(S3));
  Button button_9 (.out(S6));
  Button button_10 (.out(S9));

  // Notes on the sheet:
  //   RESET
  //   P2 MOVE
  //   P1 MOVE
  //   P1 WINS
  //   TIE
  //   P2 WINS
endmodule

module NOR_SR_Latch (
  input  R,
  input  S,
  output Q,
  output Q_prime
);

  wire clock_1_out, nor_1_out, nor_2_out;

  Clock clock_1 (.out(clock_1_out));
  nor nor_1 (nor_1_out, R, Q_prime);
  nor nor_2 (nor_2_out, Q, S);
  D_Flip_Flop d_ff_1 (.clk(clock_1_out), .D(nor_1_out), .Q(Q));  // open: Qn, preset, en, reset
  D_Flip_Flop d_ff_2 (.clk(clock_1_out), .D(nor_2_out), .Q(Q_prime));  // open: Qn, preset, en, reset
endmodule

module Cell (
  input  R,
  input  S,
  input  C,
  output CS,
  output P1,
  output P2,
  output L
);

  wire nand_1_out, nand_2_out, nor_1_out, nor_2_out, nor_3_out, nor_4_out, nor_5_out, nor_6_out, not_1_out,
       not_2_out;

  not not_1 (not_1_out, S);
  not not_2 (not_2_out, C);
  nor nor_1 (nor_1_out, not_2_out, not_1_out);
  nor nor_2 (nor_2_out, C, not_1_out);
  nor nor_3 (nor_3_out, R, nor_6_out);
  nor nor_4 (nor_4_out, nor_2_out, nor_3_out);
  nor nor_5 (nor_5_out, nor_1_out, nor_3_out);
  NOR_SR_Latch nor_sr_latch_1 (.R(nor_4_out), .S(nor_5_out), .Q(P1), .Q_prime(P2));
  nand nand_1 (nand_1_out, C, P1);
  nand nand_2 (nand_2_out, not_2_out, P2);
  nor nor_6 (nor_6_out, P2, P1);
  nand nand_3 (CS, nand_1_out, nand_2_out);
  nand nand_4 (L, nor_6_out, nor_6_out);
endmodule

module Winner (
  input  CS1,
  input  CS2,
  input  CS3,
  input  CS4,
  input  CS5,
  input  CS6,
  input  CS7,
  input  CS8,
  input  CS9,
  output out_10
);

  wire and_1_out, and_2_out, and_3_out, and_4_out, and_5_out, and_6_out, and_7_out, and_8_out;

  and and_1 (and_1_out, CS1, CS2, CS3);
  and and_2 (and_2_out, CS4, CS5, CS6);
  and and_3 (and_3_out, CS7, CS8, CS9);
  and and_4 (and_4_out, CS1, CS4, CS7);
  and and_5 (and_5_out, CS2, CS5, CS8);
  and and_6 (and_6_out, CS3, CS6, CS9);
  and and_7 (and_7_out, CS1, CS5, CS9);
  and and_8 (and_8_out, CS3, CS5, CS7);
  or or_1 (out_10, and_1_out, and_2_out, and_3_out, and_4_out, and_5_out, and_6_out, and_7_out, and_8_out);
endmodule

module Game_Over (
  input  L1,
  input  L2,
  input  L3,
  input  L4,
  input  L5,
  input  L6,
  input  L7,
  input  L8,
  input  L9,
  input  W,
  input  C,
  input  R,
  output T,
  output W1,
  output W2
);

  wire and_1_out, and_2_out, and_3_out, and_4_out, not_1_out, not_2_out, or_1_out;

  not not_1 (not_1_out, C);
  and and_1 (and_1_out, L1, L2, L3, L4, L5, L6, L7, L8, L9);
  not not_2 (not_2_out, W);
  and and_2 (and_2_out, W, C);
  and and_3 (and_3_out, not_1_out, W);
  and and_4 (and_4_out, and_1_out, not_2_out);
  LED_State led_state_1 (.W_T(and_4_out), .A(or_1_out), .R(R), .LED(T));
  LED_State led_state_2 (.W_T(and_2_out), .A(or_1_out), .R(R), .LED(W1));
  LED_State led_state_3 (.W_T(and_3_out), .A(or_1_out), .R(R), .LED(W2));
  or or_1 (or_1_out, W1, W2);
endmodule

module LED_State (
  input  W_T,
  input  A,
  input  R,
  output LED
);

  wire and_1_out, and_2_out, clock_1_out, not_1_out, not_2_out, or_1_out;

  not not_1 (not_1_out, A);
  not not_2 (not_2_out, R);
  and and_1 (and_1_out, W_T, not_1_out, not_2_out);
  and and_2 (and_2_out, A, not_2_out, LED);
  or or_1 (or_1_out, and_1_out, and_2_out);
  Clock clock_1 (.out(clock_1_out));
  D_Flip_Flop d_ff_1 (.clk(clock_1_out), .D(or_1_out), .Q(LED));  // open: Qn, preset, en, reset
endmodule
